# Fritzing sketch RaspberryPi (saved by Fritzing 0.9.6b)
breadboards: 1

parts:
  Raspberry_Pi_1 = Raspberry Pi 3 [part_number=RPI-3-V1.2]
  WeMos_D1_Mini_Relay_Shield_V1 = WeMos D1 Mini Relay Shield V2
  M1 = DC Motor  # not connected
  WeMos_D1_Mini_Relay_Shield_V2 = WeMos D1 Mini Relay Shield V2
  WeMos_D1_Mini_Relay_Shield_V3 = WeMos D1 Mini Relay Shield V2
  M2 = DC Motor  # not connected
  LED1 = smd LED [color="Red (633nm)" package="0603 [SMD]"]  # not connected

nets:
  N1: Raspberry_Pi_1.GIPO13, WeMos_D1_Mini_Relay_Shield_V3.5V
  N2: Raspberry_Pi_1.GIPO19, WeMos_D1_Mini_Relay_Shield_V2.5V
  N3: Raspberry_Pi_1.GIPO26, WeMos_D1_Mini_Relay_Shield_V1.5V
  N4: Raspberry_Pi_1.GND, WeMos_D1_Mini_Relay_Shield_V1.G
  N5: Raspberry_Pi_1.GIPO16, WeMos_D1_Mini_Relay_Shield_V2.G
  N6: Raspberry_Pi_1.GIPO12, WeMos_D1_Mini_Relay_Shield_V3.G

notes:
  Case Fan
  Extruder Fan
